# Fritzing sketch ButtonSchematic (saved by Fritzing 0.8.0b)
breadboards: 1

parts:
  Part1 = Arduino Uno (Rev3)
  S1 = Pushbutton [package=THT]
  LED1 = LED - 5mm [color="Red (633nm)" package="5 mm [THT]"]
  R1 = Resistor [tolerance=±5% resistance=220 package=THT]

nets:
  N1: Part1.GND, R1.Pin_0
  N2: Part1.D13/SCK, LED1.anode
  N3: Part1.D7, S1.leg0
  N4: Part1.5V, S1.leg1
  N5: LED1.cathode, R1.Pin_1
